# Fritzing sketch Multi-Sensor (saved by Fritzing 0.9.3b)

parts:
  U1 = attiny85 [package=dip]
  Onderdeel1 = BH1750
  M1 = BMP280
  BAT1 = CR123 battery holder [package=battery-18650-kit]
  U2 = AMS1117 step down module
  R1 = Resistor [tolerance=±5% resistance=220 package="0402 [SMD]"]
  PIR1 = PIR sensor
  U3 = FS1000A - 433Mhz RF Transmitter [package=THT]
  R2 = Resistor [tolerance=±5% resistance=220 package="0402 [SMD]"]  # not connected

nets:
  N1: U1.Pin_3, U3.DATA
  GND: U1.Pin_4, Onderdeel1.GND, M1.GND, BAT1.-, U2.GND-, R1.Pin_0, PIR1.GND
  N2: U1.Pin_5, Onderdeel1.SDA, M1.SDA
  N3: U1.Pin_6, PIR1.SIG
  N4: U1.Pin_7, Onderdeel1.SCL, M1.SCL
  VCC: U1.Pin_8, Onderdeel1.VCC, M1.VIN, U2.VOUT+, PIR1.VDD
  N5: BAT1.+, U2.VIN+

custom parts:
  BH1750: Light Sensor
  BMP280: Temperature Humidity Barometric presure Sensor, I2C
  CR123 battery holder: CR123 Battery Holder
  FS1000A - 433Mhz RF Transmitter: This is 433Mhz RF transmitter with receiver kit for Arduino ARM MCU wireless Application environment: Remote control switch, receiver module, motorcycles, automobile anti-theft products, home security products, electric doors, shutter doors, windows, remote control socket, remote control LED, remote audio remote control electric doors, garage door remote control, remote control retractable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
